# Fritzing sketch schematic (saved by Fritzing 0.9.3b)

parts:
  Raspberry_Pi_1 = Raspberry Pi 3 [part_number=RPI-3-V1.2]
  S1 = Pushbutton [package="[SMD]"]
  RE1 = Rotary Encoder [package=THT]
  RE2 = Rotary Encoder [package=THT]

nets:
  N1: Raspberry_Pi_1.GIPO4, S1.Pin_2
  N2: Raspberry_Pi_1.GIPO17, RE1.EncoderPinB
  N3: Raspberry_Pi_1.GIPO22, RE2.EncoderPinB
  N4: Raspberry_Pi_1.GIPO23, RE2.EncoderPinA
  N5: Raspberry_Pi_1.GIPO18, RE1.EncoderPinA
  N6: Raspberry_Pi_1.GND, S1.Pin_4, RE1.EncoderPinC, RE2.EncoderPinC

notes:
  Shutter Button
  Shutter Speed
  ISO
